# Fritzing sketch Distance (saved by Fritzing 0.7.11b)
breadboards: 1

parts:
  LED1 = LED - 5mm [color="Red (633nm)" package="5 mm [THT]"]
  Arduino2 = Arduino
  Part1 = SRF05 Ultrasonic Rangefinder

nets:
  GND: LED1.cathode, Arduino2.GND, Part1.GND
  N1: LED1.anode, Arduino2.D13
  N2: Arduino2.D3, Part1.Echo
  N3: Arduino2.D2, Part1.Trig
  +5V: Arduino2.+5V, Part1.VCC
