# Fritzing sketch LCD (saved by Fritzing 0.7.11b)

parts:
  Arduino1 = Arduino
  LCD1 = LCD screen

nets:
  N1: Arduino1.D12, LCD1.DB7
  N2: Arduino1.D11, LCD1.DB6
  N3: Arduino1.D10, LCD1.DB5
  N4: Arduino1.D9, LCD1.DB4

notes:
  1
  16
